// Logisim project Fluminense.circ as structural Verilog: 10 circuits, main circuit PC
module PC (
  input  [3:0] Jump_Data,
  input  Permitir_Jump,
  input  Clock,
  input  [15:0] in_4,
  input  [15:0] in_5,
  input  [15:0] in_6,
  input  [15:0] in_7,
  input  [15:0] in_8,
  input  [15:0] in_9,
  input  [15:0] in_10,
  input  [15:0] in_11,
  input  [15:0] in_12,
  input  [15:0] in_13,
  input  [15:0] in_14,
  input  [15:0] in_15,
  input  [15:0] in_16,
  input  [15:0] in_17,
  input  [15:0] in_18,
  input  [15:0] in_19,
  output [3:0] out_20,
  output [7:0] Termo,
  output [7:0] Bits
);

  wire not_1_out;

  not not_1 (not_1_out, Permitir_Jump);
  Counter #(.width(4), .max('hf)) counter_1 (
    .load(Permitir_Jump), .D(Jump_Data), .count(not_1_out), .Q(out_20), .clk(Clock));  // open: carry, clr
  Multiplexer #(.select(4), .width(16)) multiplexer_1 (
    .in0(in_4), .in1(in_5), .in2(in_6), .in3(in_7), .in4(in_8), .in5(in_9), .in6(in_10), .in7(in_11),
    .in8(in_12), .in9(in_13), .in10(in_14), .in11(in_15), .in12(in_16), .in13(in_17), .in14(in_18),
    .in15(in_19), .out({Bits, Termo}), .sel(out_20));  // open: en
endmodule

// BR
module Banco_de_Registradores (
  input  \Ativação ,
  input  [7:0] Entrada,
  input  [1:0] R1,
  input  Clock,
  input  [1:0] R2,
  output [7:0] out_6,
  output [7:0] Rs,
  output [7:0] out_8,
  output [7:0] out_9,
  output [7:0] Rt,
  output [7:0] out_11
);

  wire demultiplexer_1_out0, demultiplexer_1_out1, demultiplexer_1_out2, demultiplexer_1_out3,
       multiplexer_1_out, not_1_out, not_2_out;

  not not_1 (not_1_out, \Ativação );
  not not_2 (not_2_out, Clock);
  Multiplexer #(.disabled(0)) multiplexer_1 (
    .in0(not_2_out), .in1(1'b0), .out(multiplexer_1_out), .sel(not_1_out));  // open: en
  Demultiplexer #(.select(2)) demultiplexer_1 (
    .out0(demultiplexer_1_out0), .out1(demultiplexer_1_out1), .out2(demultiplexer_1_out2),
    .out3(demultiplexer_1_out3), .in(multiplexer_1_out), .sel(R1));  // open: en
  Register register_1 (.D(Entrada), .Q(out_6), .clk(demultiplexer_1_out0));  // open: en, clr
  Register register_2 (.D(Entrada), .Q(out_8), .clk(demultiplexer_1_out1));  // open: en, clr
  Register register_3 (.D(Entrada), .Q(out_9), .clk(demultiplexer_1_out2));  // open: en, clr
  Register register_4 (.D(Entrada), .Q(out_11), .clk(demultiplexer_1_out3));  // open: en, clr
  Multiplexer #(.select(2), .width(8)) multiplexer_2 (
    .in0(out_6), .in1(out_8), .in2(out_9), .in3(out_11), .out(Rs), .sel(R1));  // open: en
  Multiplexer #(.select(2), .width(8)) multiplexer_3 (
    .in0(out_6), .in1(out_8), .in2(out_9), .in3(out_11), .out(Rt), .sel(R2));  // open: en
endmodule

// UniC
module Unidade_de_Controle (
  input  [3:0] OP,
  input  Clock,
  output ULA,
  output Jump,
  output BR,
  output Clock_BR,
  output Clock_RAM,
  output RAM
);

  wire and_1_out, and_3_out, demultiplexer_1_out0, demultiplexer_1_out1, demultiplexer_1_out2,
       demultiplexer_1_out3, demultiplexer_1_out4, demultiplexer_1_out5, demultiplexer_1_out6,
       demultiplexer_1_out7, demultiplexer_1_out8, demultiplexer_1_out9, demultiplexer_1_out10,
       demultiplexer_1_out11, demultiplexer_1_out13, demultiplexer_1_out14, not_1_out, not_2_out, or_1_out;

  Demultiplexer #(.select(4)) demultiplexer_1 (
    .out0(demultiplexer_1_out0), .out1(demultiplexer_1_out1), .out2(demultiplexer_1_out2),
    .out3(demultiplexer_1_out3), .out4(demultiplexer_1_out4), .out5(demultiplexer_1_out5),
    .out6(demultiplexer_1_out6), .out7(demultiplexer_1_out7), .out8(demultiplexer_1_out8),
    .out9(demultiplexer_1_out9), .out10(demultiplexer_1_out10), .out11(demultiplexer_1_out11), .out12(Jump),
    .out13(demultiplexer_1_out13), .out14(demultiplexer_1_out14), .out15(RAM), .in(1'b1), .sel(OP));  // open: en
  or or_1 (or_1_out, demultiplexer_1_out13, demultiplexer_1_out14);
  or or_2 (ULA, demultiplexer_1_out2, demultiplexer_1_out3, demultiplexer_1_out4, demultiplexer_1_out5, demultiplexer_1_out6, demultiplexer_1_out7, demultiplexer_1_out8, demultiplexer_1_out9, demultiplexer_1_out10, demultiplexer_1_out11);
  not not_1 (not_1_out, demultiplexer_1_out10);
  not not_2 (not_2_out, demultiplexer_1_out11);
  and and_1 (and_1_out, Clock, or_1_out);
  and and_2 (Clock_RAM, Clock, RAM);
  and and_3 (and_3_out, ULA, not_1_out, not_2_out);
  or or_3 (BR, and_3_out, or_1_out);
  or or_4 (Clock_BR, and_3_out, and_1_out);
  // also tied to GND on the sheet: {demultiplexer_1_out0, demultiplexer_1_out1}
endmodule

// Sel.
module Seletor_de_Entrada (
  input  Sinal_ULA,
  input  Sinal_RAM,
  input  [7:0] RAM,
  input  [7:0] ULA,
  input  [7:0] Termo,
  output [7:0] \Saída 
);

  wire multiplexer_1_out;
  wire [1:0] adder_1_out, bit_extender_1_out, bit_extender_2_out;

  Multiplexer multiplexer_1 (.in0(Sinal_ULA), .in1(Sinal_RAM), .out(multiplexer_1_out), .sel(Sinal_RAM));  // open: en
  assign bit_extender_1_out = {{1{1'b0}}, multiplexer_1_out};  // Bit_Extender bit_extender_1
  assign bit_extender_2_out = {{1{1'b0}}, Sinal_RAM};  // Bit_Extender bit_extender_2
  Adder #(.width(2)) adder_1 (.a(bit_extender_1_out), .b(bit_extender_2_out), .out(adder_1_out));  // open: cin, cout
  Multiplexer #(.select(2), .width(8)) multiplexer_2 (
    .in0(Termo), .in1(ULA), .in2(RAM), .in3({8{1'b0}}), .out(\Saída ), .sel(adder_1_out));  // open: en
endmodule

// ULA - C
module ULA___Controle (
  input  [3:0] OP,
  input  [7:0] _1,
  input  [7:0] _2,
  output [7:0] out_4,
  output [7:0] out_5,
  output [7:0] out_6,
  output [7:0] \Saída ,
  output [7:0] out_8,
  output [7:0] out_9,
  output [7:0] out_10
);

  assign out_4 = _1 & _2;  // AND_Gate and_1, 8 bits wide
  assign out_5 = _1 | _2;  // OR_Gate or_1, 8 bits wide
  assign out_6 = ~(_1 & _2);  // NAND_Gate nand_1, 8 bits wide
  assign out_8 = ~(_1 | _2);  // NOR_Gate nor_1, 8 bits wide
  Adder adder_1 (.a(_1), .b(_2), .out(out_9));  // open: cin, cout
  Subtractor subtractor_1 (.a(_1), .b(_2), .out(out_10));  // open: bin, bout
  Multiplexer #(.select(4), .width(8)) multiplexer_1 (
    .in0({8{1'b0}}), .in1({8{1'b0}}), .in2(out_4), .in3(out_5), .in4(out_6), .in5(out_8), .in6(out_9),
    .in7(out_10), .in8(out_9), .in9(out_10), .in10({8{1'b0}}), .in11({8{1'b0}}), .in12({8{1'b0}}),
    .in13({8{1'b0}}), .in14({8{1'b0}}), .in15({8{1'b0}}), .out(\Saída ), .sel(OP));  // open: en
endmodule

module ULA (
  input  [3:0] OP,
  input  [7:0] _1,
  input  [7:0] _2,
  output [7:0] \Saída ,
  output \Saída_2 
);

  wire and_1_out, comparator_1_eq, multiplexer_1_out, not_1_out, not_2_out;

  Comparator comparator_1 (.a(_1), .b(_2), .eq(comparator_1_eq));  // open: gt, lt
  ULA___Controle ula_controle_1 (
    ._1(_1), ._2(_2), .OP(OP), .\Saída (\Saída ));  // open: out_9, out_10, out_4, out_5, out_6, out_8
  not not_1 (not_1_out, comparator_1_eq);
  not not_2 (not_2_out, OP[2]);
  Multiplexer multiplexer_1 (.in0(comparator_1_eq), .in1(not_1_out), .out(multiplexer_1_out), .sel(OP[0]));  // open: en
  and and_1 (and_1_out, OP[1], not_2_out, OP[3]);
  Multiplexer multiplexer_2 (.in0(1'b0), .in1(multiplexer_1_out), .out(\Saída_2 ), .sel(and_1_out));  // open: en
endmodule

module Processador (
  input  [15:0] in_1,
  input  [15:0] in_2,
  input  [15:0] in_3,
  input  [15:0] in_4,
  input  [15:0] in_5,
  input  [15:0] in_6,
  input  [15:0] in_7,
  input  [15:0] in_8,
  input  [15:0] in_9,
  input  [15:0] in_10,
  input  [15:0] in_11,
  input  [15:0] in_12,
  input  [15:0] in_13,
  input  [15:0] in_14,
  input  [15:0] in_15,
  input  [15:0] in_16,
  output [7:0] out_17,
  output [7:0] out_18,
  output [7:0] out_19,
  output [7:0] out_20,
  output [7:0] out_21,
  output [7:0] out_22,
  output [7:0] out_23,
  output [3:0] out_24,
  output [7:0] out_25,
  output [7:0] out_26,
  output [7:0] out_27
);

  wire clock_1_out, not_1_out, or_1_out, \pré_seletor_1_sinal_ram , \pré_seletor_1_sinal_ula ,
       \ula_1_saída_2 , unidade_de_controle_1_br, unidade_de_controle_1_clock_br,
       unidade_de_controle_1_clock_ram, unidade_de_controle_1_jump, unidade_de_controle_1_ram;
  wire [7:0] multiplexer_1_out, ram_1_data;

  Clock clock_1 (.out(clock_1_out));
  or or_1 (or_1_out, \ula_1_saída_2 , unidade_de_controle_1_jump);
  PC pc_1 (
    .Jump_Data(out_26[7:4]), .Permitir_Jump(or_1_out), .Clock(clock_1_out), .in_4(in_1), .in_5(in_2),
    .in_6(in_3), .in_7(in_4), .in_8(in_5), .in_9(in_6), .in_10(in_7), .in_11(in_8), .in_12(in_9),
    .in_13(in_10), .in_14(in_11), .in_15(in_12), .in_16(in_13), .in_17(in_14), .in_18(in_15), .in_19(in_16),
    .out_20(out_24), .Termo(out_26), .Bits(out_27));
  Unidade_de_Controle unidade_de_controle_1 (
    .OP(out_27[7:4]), .Clock(clock_1_out), .Jump(unidade_de_controle_1_jump), .BR(unidade_de_controle_1_br),
    .Clock_BR(unidade_de_controle_1_clock_br), .Clock_RAM(unidade_de_controle_1_clock_ram),
    .RAM(unidade_de_controle_1_ram));  // open: ULA
  not not_1 (not_1_out, unidade_de_controle_1_ram);
  Banco_de_Registradores banco_de_registradores_1 (
    .R1(out_27[3:2]), .Clock(unidade_de_controle_1_clock_br), .R2(out_27[1:0]),
    .\Ativação (unidade_de_controle_1_br), .Entrada(out_17), .out_6(out_18), .out_8(out_19), .out_9(out_20),
    .out_11(out_22), .Rs(out_23), .Rt(out_25));
  Multiplexer #(.width(8)) multiplexer_1 (.in0(out_26), .out(multiplexer_1_out), .sel(out_27[5]));  // open: in1, en
  RAM ram_1 (
    .addr(out_26), .data(ram_1_data), .clk(unidade_de_controle_1_clock_ram), .ld(not_1_out));  // open: sel, clr
  \Pré_Seletor  \pré_seletor_1  (
    .OP(out_27[7:4]), .Sinal_ULA(\pré_seletor_1_sinal_ula ), .Sinal_RAM(\pré_seletor_1_sinal_ram ));
  assign ram_1_data = unidade_de_controle_1_ram ? out_23 : 8'bz;  // Controlled_Buffer controlled_buffer_1
  Seletor_de_Entrada seletor_de_entrada_1 (
    .Sinal_ULA(\pré_seletor_1_sinal_ula ), .Sinal_RAM(\pré_seletor_1_sinal_ram ), .\Saída (out_17),
    .RAM(out_26), .ULA(out_21), .Termo(ram_1_data));
  ULA ula_1 (._1(out_23), ._2(multiplexer_1_out), .OP(out_27[7:4]), .\Saída (out_21), .\Saída_2 (\ula_1_saída_2 ));
endmodule

// P-Sl
module \Pré_Seletor  (
  input  [3:0] OP,
  output Sinal_ULA,
  output Sinal_RAM
);

  wire and_1_out, not_1_out, not_2_out, not_3_out;

  not not_1 (not_1_out, OP[0]);
  not not_2 (not_2_out, OP[1]);
  and and_1 (and_1_out, not_1_out, OP[1], OP[2], OP[3]);
  not not_3 (not_3_out, and_1_out);
  and and_2 (Sinal_RAM, OP[0], not_2_out, OP[2], OP[3]);
  Multiplexer #(.select(4)) multiplexer_1 (
    .in0(1'b0), .in1(not_3_out), .in2(not_3_out), .in3(not_3_out), .in4(not_3_out), .in5(not_3_out),
    .in6(not_3_out), .in7(not_3_out), .in8(not_3_out), .in9(not_3_out), .in10(not_3_out), .in11(not_3_out),
    .in12(not_3_out), .in13(not_3_out), .in14(not_3_out), .in15(not_3_out), .out(Sinal_ULA), .sel(OP));  // open: en
endmodule

// RAM
module \Memória_RAM  (
  input  [3:0] Index,
  input  Ler_0___Esc_1,
  input  [1:0] Array,
  input  Set,
  input  Reset,
  input  [15:0] Input,
  input  Clock,
  output [15:0] Output
);

  wire demultiplexer_1_out0, demultiplexer_1_out1, demultiplexer_1_out2, demultiplexer_1_out3,
       demultiplexer_1_out4, demultiplexer_1_out5, demultiplexer_1_out6, demultiplexer_1_out7,
       demultiplexer_1_out8, demultiplexer_1_out9, demultiplexer_1_out10, demultiplexer_1_out11,
       demultiplexer_1_out12, demultiplexer_1_out13, demultiplexer_1_out14, demultiplexer_1_out15,
       multiplexer_1_out;
  wire [15:0] multiplexer_2_out, \valor_de_memória_16_bits_1_output , \valor_de_memória_16_bits_2_output ,
       \valor_de_memória_16_bits_3_output , \valor_de_memória_16_bits_4_output ,
       \valor_de_memória_16_bits_5_output , \valor_de_memória_16_bits_6_output ,
       \valor_de_memória_16_bits_7_output , \valor_de_memória_16_bits_8_output ,
       \valor_de_memória_16_bits_9_output , \valor_de_memória_16_bits_10_output ,
       \valor_de_memória_16_bits_11_output , \valor_de_memória_16_bits_12_output ,
       \valor_de_memória_16_bits_13_output , \valor_de_memória_16_bits_14_output ,
       \valor_de_memória_16_bits_15_output , \valor_de_memória_16_bits_16_output ;

  Multiplexer multiplexer_1 (.in0(1'b0), .in1(Clock), .out(multiplexer_1_out), .sel(Ler_0___Esc_1));  // open: en
  Demultiplexer #(.select(4)) demultiplexer_1 (
    .out0(demultiplexer_1_out0), .out1(demultiplexer_1_out1), .out2(demultiplexer_1_out2),
    .out3(demultiplexer_1_out3), .out4(demultiplexer_1_out4), .out5(demultiplexer_1_out5),
    .out6(demultiplexer_1_out6), .out7(demultiplexer_1_out7), .out8(demultiplexer_1_out8),
    .out9(demultiplexer_1_out9), .out10(demultiplexer_1_out10), .out11(demultiplexer_1_out11),
    .out12(demultiplexer_1_out12), .out13(demultiplexer_1_out13), .out14(demultiplexer_1_out14),
    .out15(demultiplexer_1_out15), .in(multiplexer_1_out), .sel({Array, Index[1:0]}));  // open: en
  \Valor_de_memória_16_bits  \valor_de_memória_16_bits_1  (
    .Input(Input), .Clock(demultiplexer_1_out0), .SET(Set), .RESET(Reset),
    .Output(\valor_de_memória_16_bits_1_output ));
  \Valor_de_memória_16_bits  \valor_de_memória_16_bits_2  (
    .Input(Input), .Clock(demultiplexer_1_out1), .SET(Set), .RESET(Reset),
    .Output(\valor_de_memória_16_bits_2_output ));
  \Valor_de_memória_16_bits  \valor_de_memória_16_bits_3  (
    .Input(Input), .Clock(demultiplexer_1_out2), .SET(Set), .RESET(Reset),
    .Output(\valor_de_memória_16_bits_3_output ));
  \Valor_de_memória_16_bits  \valor_de_memória_16_bits_4  (
    .Input(Input), .Clock(demultiplexer_1_out3), .SET(Set), .RESET(Reset),
    .Output(\valor_de_memória_16_bits_4_output ));
  \Valor_de_memória_16_bits  \valor_de_memória_16_bits_5  (
    .Input(Input), .Clock(demultiplexer_1_out4), .SET(Set), .RESET(Reset),
    .Output(\valor_de_memória_16_bits_5_output ));
  \Valor_de_memória_16_bits  \valor_de_memória_16_bits_6  (
    .Input(Input), .Clock(demultiplexer_1_out5), .SET(Set), .RESET(Reset),
    .Output(\valor_de_memória_16_bits_6_output ));
  \Valor_de_memória_16_bits  \valor_de_memória_16_bits_7  (
    .Input(Input), .Clock(demultiplexer_1_out6), .SET(Set), .RESET(Reset),
    .Output(\valor_de_memória_16_bits_7_output ));
  \Valor_de_memória_16_bits  \valor_de_memória_16_bits_8  (
    .Input(Input), .Clock(demultiplexer_1_out7), .SET(Set), .RESET(Reset),
    .Output(\valor_de_memória_16_bits_8_output ));
  \Valor_de_memória_16_bits  \valor_de_memória_16_bits_9  (
    .Input(Input), .Clock(demultiplexer_1_out8), .SET(Set), .RESET(Reset),
    .Output(\valor_de_memória_16_bits_9_output ));
  \Valor_de_memória_16_bits  \valor_de_memória_16_bits_10  (
    .Input(Input), .Clock(demultiplexer_1_out9), .SET(Set), .RESET(Reset),
    .Output(\valor_de_memória_16_bits_10_output ));
  \Valor_de_memória_16_bits  \valor_de_memória_16_bits_11  (
    .Input(Input), .Clock(demultiplexer_1_out10), .SET(Set), .RESET(Reset),
    .Output(\valor_de_memória_16_bits_11_output ));
  \Valor_de_memória_16_bits  \valor_de_memória_16_bits_12  (
    .Input(Input), .Clock(demultiplexer_1_out11), .SET(Set), .RESET(Reset),
    .Output(\valor_de_memória_16_bits_12_output ));
  \Valor_de_memória_16_bits  \valor_de_memória_16_bits_13  (
    .Input(Input), .Clock(demultiplexer_1_out12), .SET(Set), .RESET(Reset),
    .Output(\valor_de_memória_16_bits_13_output ));
  \Valor_de_memória_16_bits  \valor_de_memória_16_bits_14  (
    .Input(Input), .Clock(demultiplexer_1_out13), .SET(Set), .RESET(Reset),
    .Output(\valor_de_memória_16_bits_14_output ));
  \Valor_de_memória_16_bits  \valor_de_memória_16_bits_15  (
    .Input(Input), .Clock(demultiplexer_1_out14), .SET(Set), .RESET(Reset),
    .Output(\valor_de_memória_16_bits_15_output ));
  \Valor_de_memória_16_bits  \valor_de_memória_16_bits_16  (
    .Input(Input), .Clock(demultiplexer_1_out15), .SET(Set), .RESET(Reset),
    .Output(\valor_de_memória_16_bits_16_output ));
  // Probe on \valor_de_memória_16_bits_1_output 
  // Probe on \valor_de_memória_16_bits_2_output 
  // Probe on \valor_de_memória_16_bits_3_output 
  // Probe on \valor_de_memória_16_bits_4_output 
  // Probe on \valor_de_memória_16_bits_5_output 
  // Probe on \valor_de_memória_16_bits_6_output 
  // Probe on \valor_de_memória_16_bits_7_output 
  // Probe on \valor_de_memória_16_bits_8_output 
  // Probe on \valor_de_memória_16_bits_9_output 
  // Probe on \valor_de_memória_16_bits_10_output 
  // Probe on \valor_de_memória_16_bits_11_output 
  // Probe on \valor_de_memória_16_bits_12_output 
  // Probe on \valor_de_memória_16_bits_13_output 
  // Probe on \valor_de_memória_16_bits_14_output 
  // Probe on \valor_de_memória_16_bits_15_output 
  // Probe on \valor_de_memória_16_bits_16_output 
  Multiplexer #(.select(4), .width(16)) multiplexer_2 (
    .in0(\valor_de_memória_16_bits_1_output ), .in1(\valor_de_memória_16_bits_2_output ),
    .in2(\valor_de_memória_16_bits_3_output ), .in3(\valor_de_memória_16_bits_4_output ),
    .in4(\valor_de_memória_16_bits_5_output ), .in5(\valor_de_memória_16_bits_6_output ),
    .in6(\valor_de_memória_16_bits_7_output ), .in7(\valor_de_memória_16_bits_8_output ),
    .in8(\valor_de_memória_16_bits_9_output ), .in9(\valor_de_memória_16_bits_10_output ),
    .in10(\valor_de_memória_16_bits_11_output ), .in11(\valor_de_memória_16_bits_12_output ),
    .in12(\valor_de_memória_16_bits_13_output ), .in13(\valor_de_memória_16_bits_14_output ),
    .in14(\valor_de_memória_16_bits_15_output ), .in15(\valor_de_memória_16_bits_16_output ),
    .out(multiplexer_2_out), .sel({Array, Index[1:0]}));  // open: en
  Multiplexer #(.width(16)) multiplexer_3 (
    .in0(multiplexer_2_out), .in1({16{1'b0}}), .out(Output), .sel(Ler_0___Esc_1));  // open: en
endmodule

// VM
module \Valor_de_memória_16_bits  (
  input  RESET,
  input  SET,
  input  [15:0] Input,
  input  Clock,
  output [15:0] Output
);

  D_Flip_Flop d_ff_1 (.clk(Clock), .D(Input[0]), .Q(Output[0]), .preset(SET), .reset(RESET));  // open: Qn, en
  D_Flip_Flop d_ff_2 (.clk(Clock), .D(Input[1]), .Q(Output[1]), .preset(SET), .reset(RESET));  // open: Qn, en
  D_Flip_Flop d_ff_3 (.clk(Clock), .D(Input[2]), .Q(Output[2]), .preset(SET), .reset(RESET));  // open: Qn, en
  D_Flip_Flop d_ff_4 (.clk(Clock), .D(Input[3]), .Q(Output[3]), .preset(SET), .reset(RESET));  // open: Qn, en
  D_Flip_Flop d_ff_5 (.clk(Clock), .D(Input[4]), .Q(Output[4]), .preset(SET), .reset(RESET));  // open: Qn, en
  D_Flip_Flop d_ff_6 (.clk(Clock), .D(Input[5]), .Q(Output[5]), .preset(SET), .reset(RESET));  // open: Qn, en
  D_Flip_Flop d_ff_7 (.clk(Clock), .D(Input[6]), .Q(Output[6]), .preset(SET), .reset(RESET));  // open: Qn, en
  D_Flip_Flop d_ff_8 (.clk(Clock), .D(Input[7]), .Q(Output[7]), .preset(SET), .reset(RESET));  // open: Qn, en
  D_Flip_Flop d_ff_9 (.clk(Clock), .D(Input[8]), .Q(Output[8]), .preset(SET), .reset(RESET));  // open: Qn, en
  D_Flip_Flop d_ff_10 (.clk(Clock), .D(Input[9]), .Q(Output[9]), .preset(SET), .reset(RESET));  // open: Qn, en
  D_Flip_Flop d_ff_11 (.clk(Clock), .D(Input[10]), .Q(Output[10]), .preset(SET), .reset(RESET));  // open: Qn, en
  D_Flip_Flop d_ff_12 (.clk(Clock), .D(Input[11]), .Q(Output[11]), .preset(SET), .reset(RESET));  // open: Qn, en
  D_Flip_Flop d_ff_13 (.clk(Clock), .D(Input[12]), .Q(Output[12]), .preset(SET), .reset(RESET));  // open: Qn, en
  D_Flip_Flop d_ff_14 (.clk(Clock), .D(Input[13]), .Q(Output[13]), .preset(SET), .reset(RESET));  // open: Qn, en
  D_Flip_Flop d_ff_15 (.clk(Clock), .D(Input[14]), .Q(Output[14]), .preset(SET), .reset(RESET));  // open: Qn, en
  D_Flip_Flop d_ff_16 (.clk(Clock), .D(Input[15]), .Q(Output[15]), .preset(SET), .reset(RESET));  // open: Qn, en
endmodule
